# Fritzing sketch arduino_reset_t124 (saved by Fritzing 0.9.2b)
circuit board: 8.46667cm x 5.64444cm
breadboards: 1

parts:
  Q2 = NPN-Transistor [part_number=BC548B package="TO92 [THT]"]
  Pro_Micro_3_3v = SparkFun Pro Micro
  Reset_Jetson_TK1 = Momentary Switch [package=ksa_sealed_tac_switch]
  Force_Recovery_Jetson_TK1 = Momentary Switch [package=ksa_sealed_tac_switch]
  Q1 = NPN-Transistor [part_number=BC548B package="TO92 [THT]"]

nets:
  N1: Q2.E, Force_Recovery_Jetson_TK1.1
  N2: Q2.B, Pro_Micro_3_3v.9
  N3: Q2.C, Reset_Jetson_TK1.3, Q1.C
  N4: Pro_Micro_3_3v.3, Pro_Micro_3_3v.4
  N5: Pro_Micro_3_3v.10, Q1.B
  N6: Reset_Jetson_TK1.2, Q1.E

custom parts:
  SparkFun Pro Micro: The Pro Micro is similar to the Pro Mini except with an ATmega32U4 on board. The USB transceiver inside the 32U4 allows us to add USB connectivity on-board and do away with bulky external USB interface. Based on: https://github.com/unorthodox-engineers/unorthodox-arduino/blob/master/Unorthodox/fritzing/parts/Pro%20Micro.fzpz
